// Logisim project Aux1.circ as structural Verilog: 9 circuits, main circuit SegD
module SegD (
  input  x3,
  input  x2,
  input  x1,
  input  x0,
  output d
);

  wire and_1_out, and_2_out, and_3_out, and_4_out, not_1_out, not_2_out, not_3_out;

  not not_1 (not_1_out, x0);
  not not_2 (not_2_out, x1);
  not not_3 (not_3_out, x2);
  and and_1 (and_1_out, x2, not_2_out, x0);
  and and_2 (and_2_out, not_1_out, x1);
  and and_3 (and_3_out, not_3_out, x1);
  and and_4 (and_4_out, not_3_out, not_1_out);
  or or_1 (d, x3, and_1_out, and_2_out, and_3_out, and_4_out);
endmodule

module _7segms (
  input  x3,
  input  x2,
  input  x1,
  input  x0,
  output a,
  output f,
  output b,
  output g,
  output e,
  output c,
  output d
);

  SegF segf_1 (.x3(x3), .x2(x2), .x1(x1), .x0(x0), .out_5(f));
  SegE sege_1 (.x3(x3), .x2(x2), .x1(x1), .x0(x0), .out_5(e));
  SegA u_a (.x3(x3), .x2(x2), .x1(x1), .x0(x0), .out_5(a));
  SegB u_b (.x3(x3), .x2(x2), .x1(x1), .x0(x0), .out_5(b));
  SegC u_c (.x3(x3), .x2(x2), .x1(x1), .x0(x0), .out_5(c));
  SegD segd_1 (.x3(x3), .x2(x2), .x1(x1), .x0(x0), .d(d));
  SegG segg_1 (.x3(x3), .x2(x2), .x1(x1), .x0(x0), .out_5(g));
endmodule

module SegA (
  input  x3,
  input  x2,
  input  x1,
  input  x0,
  output out_5
);

  wire and_1_out, and_2_out, not_1_out, not_2_out;

  not not_1 (not_1_out, x0);
  not not_2 (not_2_out, x2);
  and and_1 (and_1_out, not_2_out, not_1_out);
  and and_2 (and_2_out, x2, x0);
  or or_1 (out_5, x3, and_1_out, x1, and_2_out);
endmodule

module SegB (
  input  x3,
  input  x2,
  input  x1,
  input  x0,
  output out_5
);

  wire and_1_out, and_2_out, not_1_out, not_2_out, not_3_out;

  not not_1 (not_1_out, x2);
  not not_2 (not_2_out, x0);
  not not_3 (not_3_out, x1);
  and and_1 (and_1_out, not_3_out, not_2_out);
  and and_2 (and_2_out, x1, x0);
  or or_1 (out_5, not_1_out, and_1_out, and_2_out);
endmodule

module SegC (
  input  x3,
  input  x2,
  input  x1,
  input  x0,
  output out_5
);

  wire not_1_out;

  not not_1 (not_1_out, x1);
  or or_1 (out_5, x2, not_1_out, x0);
endmodule

module SegE (
  input  x3,
  input  x2,
  input  x1,
  input  x0,
  output out_5
);

  wire and_1_out, and_2_out, not_1_out, not_2_out;

  not not_1 (not_1_out, x2);
  not not_2 (not_2_out, x0);
  and and_1 (and_1_out, not_1_out, not_2_out);
  and and_2 (and_2_out, x1, not_2_out);
  or or_1 (out_5, and_1_out, and_2_out);
endmodule

module SegF (
  input  x3,
  input  x2,
  input  x1,
  input  x0,
  output out_5
);

  wire and_1_out, and_2_out, and_3_out, not_1_out, not_2_out;

  not not_1 (not_1_out, x1);
  not not_2 (not_2_out, x0);
  and and_1 (and_1_out, x2, not_1_out);
  and and_2 (and_2_out, x2, not_2_out);
  and and_3 (and_3_out, not_1_out, not_2_out);
  or or_1 (out_5, x3, and_1_out, and_2_out, and_3_out);
endmodule

module SegG (
  input  x3,
  input  x2,
  input  x1,
  input  x0,
  output out_5
);

  wire and_1_out, and_2_out, and_3_out, not_1_out, not_2_out, not_3_out;

  not not_1 (not_1_out, x0);
  not not_2 (not_2_out, x2);
  not not_3 (not_3_out, x1);
  and and_1 (and_1_out, not_2_out, x1);
  and and_2 (and_2_out, x2, not_3_out);
  and and_3 (and_3_out, x1, not_1_out);
  or or_1 (out_5, x3, and_1_out, and_2_out, and_3_out);
endmodule

module _7Segmens2 (
  input  x3,
  input  x2,
  input  x1,
  input  x0
);

  wire n7segms_1_a, n7segms_1_d, n7segms_1_g;
  wire [3:3] n7segms_1_b, n7segms_1_c, n7segms_1_e, n7segms_1_f;

  _7segms u_7segms_1 (
    .x3(x3), .x2(x2), .x1(x1), .x0(x0), .b(n7segms_1_b[3]), .g(n7segms_1_g), .c(n7segms_1_c[3]),
    .d(n7segms_1_d), .a(n7segms_1_a), .f(n7segms_1_f[3]), .e(n7segms_1_e[3]));
  DotMatrix #(.matrixcols(4), .matrixrows(1)) dotmatrix_1 (
    .col0(n7segms_1_a), .col1(n7segms_1_a), .col2(n7segms_1_a), .col3(n7segms_1_a));
  DotMatrix #(.matrixcols(1), .matrixrows(4)) dotmatrix_2 (.col0({4{n7segms_1_f[3]}}));
  DotMatrix #(.matrixcols(4), .matrixrows(1)) dotmatrix_3 (
    .col0(n7segms_1_g), .col1(n7segms_1_g), .col2(n7segms_1_g), .col3(n7segms_1_g));
  DotMatrix #(.matrixcols(1), .matrixrows(4)) dotmatrix_4 (.col0({4{n7segms_1_e[3]}}));
  DotMatrix #(.matrixcols(4), .matrixrows(1)) dotmatrix_5 (
    .col0(n7segms_1_d), .col1(n7segms_1_d), .col2(n7segms_1_d), .col3(n7segms_1_d));
  DotMatrix #(.matrixcols(1), .matrixrows(4)) dotmatrix_6 (.col0({4{n7segms_1_b[3]}}));
  DotMatrix #(.matrixcols(1), .matrixrows(4)) dotmatrix_7 (.col0({4{n7segms_1_c[3]}}));
endmodule
